# Fritzing sketch Talking_Drum_electronics (saved by Fritzing 0.9.3b)

parts:
  Solenoid_-_L1 = Solenoid
  Drum_pushbutton_S1 = Round Pushbutton
  Pitch_potentiometer = Rotary Potentiometer (Large) [maximum_resistance=100kΩ package=THT]
  Big_Easy_Stepper_Motor_Driver_1 = EasyDriver_v44 [part_number="Sparkfun ROB-12859"]
  J1_-_12_volts = Power Jack [package=power_jack_pth]
  Stepper_Motor_1 = Stepper Motor - Bipolar [part_number="Sparkfun ROB-10846"]
  Stepper_Motor_2 = Stepper Motor - Bipolar [part_number="Sparkfun ROB-10846"]
  Big_Easy_Stepper_Motor_Driver_2 = EasyDriver_v44 [part_number="Sparkfun ROB-12859"]
  R2 = Resistor [tolerance=±5% resistance=100k package=THT]
  N-MOSFET = MOSFET-NCHANNEL [part_number=IRFZ44N package=to220v]
  R3 = Resistor [tolerance=±5% resistance=29 package="1206 [SMD]"]
  R4 = Resistor [tolerance=±5% resistance=100k package="1206 [SMD]"]
  D1 = Diode [package=sma-diode-kit]
  Arduino_Uno = Arduino Uno (Rev3)

nets:
  N1: Solenoid_-_L1.pin1, Big_Easy_Stepper_Motor_Driver_2.V+, D1.C
  N2: Solenoid_-_L1.pin2, N-MOSFET.D, D1.A
  GND: Drum_pushbutton_S1.leg0, J1_-_12_volts.GND, N-MOSFET.S, R4.Pin_1, Arduino_Uno.GND
  N3: Drum_pushbutton_S1.leg1, R2.Pin_1, Arduino_Uno.D3_PWM
  N4: Pitch_potentiometer.wiper, Arduino_Uno.A0
  VCC: Pitch_potentiometer.leg2, Big_Easy_Stepper_Motor_Driver_1.VCC, Big_Easy_Stepper_Motor_Driver_2.VCC, R2.Pin_0, Arduino_Uno.5V
  GND_2: Big_Easy_Stepper_Motor_Driver_1.GND, Big_Easy_Stepper_Motor_Driver_2.GND
  N5: Big_Easy_Stepper_Motor_Driver_1.V+, J1_-_12_volts.PWR
  N6: Big_Easy_Stepper_Motor_Driver_1.STEP, Arduino_Uno.D9_PWM
  N7: Big_Easy_Stepper_Motor_Driver_1.DIR, Arduino_Uno.D8
  N8: Big_Easy_Stepper_Motor_Driver_1.OUT2A, Stepper_Motor_1.D
  N9: Big_Easy_Stepper_Motor_Driver_1.OUT2B, Stepper_Motor_1.B
  N10: Big_Easy_Stepper_Motor_Driver_1.OUT1A, Stepper_Motor_1.A
  N11: Big_Easy_Stepper_Motor_Driver_1.OUT1B, Stepper_Motor_1.C
  N12: Stepper_Motor_2.A, Big_Easy_Stepper_Motor_Driver_2.OUT1A
  N13: Stepper_Motor_2.C, Big_Easy_Stepper_Motor_Driver_2.OUT1B
  N14: Stepper_Motor_2.B, Big_Easy_Stepper_Motor_Driver_2.OUT2B
  N15: Stepper_Motor_2.D, Big_Easy_Stepper_Motor_Driver_2.OUT2A
  N16: Big_Easy_Stepper_Motor_Driver_2.STEP, Arduino_Uno.D13/SCK
  N17: Big_Easy_Stepper_Motor_Driver_2.DIR, Arduino_Uno.D12/MISO
  N18: N-MOSFET.G, R3.Pin_1, R4.Pin_0
  N19: R3.Pin_0, Arduino_Uno.D2
